// Logisim project jrmips.circ as structural Verilog
module main (
  output [15:0] out_1
);

  wire button_1_out, clock_1_out, control2_1_immediate, control2_1_pc, control2_1_rs, control2_1_shamt,
       control2_1_writeenable, control_1_halt, control_1_i_value, control_1_memorysignal, control_1_put,
       control_1_shiftsignal, control_3_1__0sign, control_3_1_jumpandlink, control_3_1_load,
       control_3_1_shiftright, control_3_1_store, not_1_out;
  wire [2:0] control_1_rs, control_1_rt;
  wire [3:0] ALU_less, control_1_shift_amount, multiplexer_1_out;
  wire [4:0] control_1_opcode;
  wire [7:0] adder_1_out, control_1_immediate, controlled_buffer_1_out, PC_q;
  wire [15:0] ALU_output, bit_extender_1_out, bit_extender_2_out, bit_extender_3_out,
       controlled_buffer_4_out, multiplexer_2_out, multiplexer_3_out, multiplexer_4_out, multiplexer_5_out,
       multiplexer_6_out, multiplexer_7_out, ram_1_data, Register_File_read_data2, rom_1_data, shifter_1_out,
       shifter_2_out;

  not not_1 (not_1_out, control_1_halt);
  LED halt (.in(control_1_halt));
  Register PC (.D(controlled_buffer_1_out), .en(not_1_out), .Q(PC_q), .clk(clock_1_out), .clr(button_1_out));
  Clock clock_1 (.out(clock_1_out));
  assign controlled_buffer_1_out = control2_1_pc ? adder_1_out : 8'bz;  // Controlled_Buffer controlled_buffer_1
  assign controlled_buffer_1_out = control2_1_immediate ? control_1_immediate : 8'bz;  // Controlled_Buffer controlled_buffer_2
  Adder adder_1 (.a(8'h1), .b(PC_q), .out(adder_1_out));  // open: cin, cout
  Button button_1 (.out(button_1_out));
  assign controlled_buffer_1_out = control2_1_rs ? out_1[7:0] : 8'bz;  // Controlled_Buffer controlled_buffer_3
  ROM #(.dataWidth(16)) rom_1 (.addr(PC_q), .data(rom_1_data));  // open: sel
  Control2 control2_1 (
    .in_1(rom_1_data), .in_2(ALU_less), .Immediate(control2_1_immediate), .PC(control2_1_pc),
    .RS(control2_1_rs), .shamt(control2_1_shamt), .writeenable(control2_1_writeenable));
  Control control_1 (
    .in_1(rom_1_data), .Rs(control_1_rs), .Rt(control_1_rt), .Immediate(control_1_immediate),
    .Shift_amount(control_1_shift_amount), .I_value(control_1_i_value), .Opcode(control_1_opcode),
    .shiftsignal(control_1_shiftsignal), .memorysignal(control_1_memorysignal), .halt(control_1_halt),
    .put(control_1_put));
  Control_3 control_3_1 (
    .in_1(rom_1_data), .store(control_3_1_store), .load(control_3_1_load),
    .jumpandlink(control_3_1_jumpandlink), .shiftright(control_3_1_shiftright), ._0sign(control_3_1__0sign));  // open: out_2
  assign bit_extender_1_out = {{8{1'b0}}, control_1_immediate};  // Bit_Extender bit_extender_1
  assign bit_extender_2_out = {{8{control_1_immediate[7]}}, control_1_immediate};  // Bit_Extender bit_extender_2
  Register_File Register_File (
    .WriteEnable(control2_1_writeenable), .ReadRegister1(control_1_rs), .ReadRegister2(control_1_rt),
    .Write_Register(control_1_rs), .WriteData(multiplexer_6_out), .clock(clock_1_out), .Read_Data1(out_1),
    .Read_Data2(Register_File_read_data2));
  Multiplexer #(.width(4), .enable("false")) multiplexer_1 (
    .in0(Register_File_read_data2[3:0]), .in1(control_1_shift_amount), .out(multiplexer_1_out),
    .sel(control2_1_shamt));
  Multiplexer #(.width(16), .enable("false")) multiplexer_2 (
    .in0(bit_extender_2_out), .in1(bit_extender_1_out), .out(multiplexer_2_out), .sel(control_3_1__0sign));
  Multiplexer #(.width(16), .enable("false")) multiplexer_3 (
    .in0(Register_File_read_data2), .in1(multiplexer_2_out), .out(multiplexer_3_out), .sel(control_1_i_value));
  Shifter #(.width(16)) shifter_1 (.in(out_1), .\dist (multiplexer_1_out), .out(shifter_1_out));
  Shifter #(.width(16), .shift("lr")) shifter_2 (.in(out_1), .\dist (multiplexer_1_out), .out(shifter_2_out));
  assign controlled_buffer_4_out = control_1_put ? out_1 : 16'bz;  // Controlled_Buffer controlled_buffer_4
  ALU ALU (
    .Input_1(out_1), .Input_2(multiplexer_3_out), .Opcode(control_1_opcode), .Output(ALU_output),
    .greater(ALU_less[1]), .zero(ALU_less[3]), .less(ALU_less[0]), .notzero(ALU_less[2]));
  Multiplexer #(.width(16), .enable("false")) multiplexer_4 (
    .in0(shifter_1_out), .in1(shifter_2_out), .out(multiplexer_4_out), .sel(control_3_1_shiftright));
  Hex_Digit_Display hex_digit_display_1 (.value(controlled_buffer_4_out[15:12]));  // open: dp
  Multiplexer #(.width(16), .enable("false")) multiplexer_5 (
    .in0(ALU_output), .in1(multiplexer_4_out), .out(multiplexer_5_out), .sel(control_1_shiftsignal));
  Hex_Digit_Display hex_digit_display_2 (.value(controlled_buffer_4_out[11:8]));  // open: dp
  Hex_Digit_Display hex_digit_display_3 (.value(controlled_buffer_4_out[3:0]));  // open: dp
  Hex_Digit_Display hex_digit_display_4 (.value(controlled_buffer_4_out[7:4]));  // open: dp
  RAM #(.dataWidth(16), .bus("separate")) ram_1 (
    .addr(Register_File_read_data2[7:0]), .din(out_1), .data(ram_1_data), .str(control_3_1_store),
    .clk(clock_1_out), .ld(control_3_1_load));  // open: sel, clr
  Multiplexer #(.width(16), .enable("false")) multiplexer_6 (
    .in0(multiplexer_7_out), .in1(bit_extender_3_out), .out(multiplexer_6_out), .sel(control_3_1_jumpandlink));
  assign bit_extender_3_out = {{8{1'b0}}, adder_1_out};  // Bit_Extender bit_extender_3
  Multiplexer #(.width(16), .enable("false")) multiplexer_7 (
    .in0(multiplexer_5_out), .in1(ram_1_data), .out(multiplexer_7_out), .sel(control_1_memorysignal));

  // Notes on the sheet:
  //   Andrew Beers
  //   acb75
  //   contents of rom_1 (hex, n*v repeats v):
  //   2 c000 1fc c000
endmodule

module Fetch (
);

  wire clock_1_out;
  wire [3:0] control_1_shift_amount;
  wire [7:0] adder_1_out, control_1_immediate, register_1_q;
  wire [15:0] undriven;

  Clock clock_1 (.out(clock_1_out));
  Register register_1 (.D(adder_1_out), .Q(register_1_q), .clk(clock_1_out));  // open: en, clr
  Adder adder_1 (.a(8'h1), .b(register_1_q), .out(adder_1_out));  // open: cin, cout
  Instruction_Addresses instruction_addresses_1 (.in_1(undriven));
  LED led_1 (.in(register_1_q[0]));
  LED led_2 (.in(register_1_q[1]));
  LED led_3 (.in(register_1_q[2]));
  LED led_4 (.in(register_1_q[3]));
  LED led_5 (.in(register_1_q[4]));
  LED led_6 (.in(register_1_q[5]));
  LED led_7 (.in(register_1_q[6]));
  LED led_8 (.in(register_1_q[7]));
  Control control_1 (
    .Immediate(control_1_immediate), .Shift_amount(control_1_shift_amount));  // open: in_1, Rs, Rt, I_value, Opcode, shiftsignal, memorysignal, halt, put
endmodule

// Control 2
module Control (
  input  [15:0] in_1,
  output [2:0] Rs,
  output [2:0] Rt,
  output [7:0] Immediate,
  output [3:0] Shift_amount,
  output I_value,
  output [4:0] Opcode,
  output shiftsignal,
  output memorysignal,
  output halt,
  output put
);

  Opcode_Combinational opcode_combinational_1 (
    .A(in_1[15]), .B(in_1[14]), .C(in_1[13]), .D(in_1[12]), .E(in_1[0]), .I(I_value));  // open: R
  halt halt_1 (.a(in_1[15]), .b(in_1[14]), .c(in_1[13]), .d(in_1[12]), .e(in_1[0]), .shift(halt));
  memorysignal memorysignal_1 (.a(in_1[15]), .b(in_1[14]), .c(in_1[13]), .d(in_1[12]), .shift(memorysignal));
  putsignal putsignal_1 (.a(in_1[15]), .b(in_1[14]), .c(in_1[13]), .d(in_1[12]), .e(in_1[0]), .shift(put));
  ShiftSignal shiftsignal_1 (.a(in_1[15]), .b(in_1[14]), .c(in_1[13]), .d(in_1[12]), .shift(shiftsignal));

  assign Immediate = in_1[8:1];
  assign Opcode = {in_1[15:12], in_1[0]};
  assign Rs = in_1[11:9];
  assign Rt = in_1[8:6];
  assign Shift_amount = in_1[4:1];
endmodule

module Opcode_Combinational (
  input  A,
  input  B,
  input  C,
  input  D,
  input  E,
  output I,
  output R
);

  wire and_1_out, and_2_out, and_3_out, and_4_out, and_5_out, and_6_out, and_7_out, and_8_out, and_9_out,
       and_10_out, and_11_out, and_12_out, not_1_out, not_2_out, not_3_out, not_4_out, not_5_out, not_6_out,
       not_7_out, not_8_out, or_1_out, or_2_out, or_3_out;

  not not_1 (not_1_out, B);
  not not_2 (not_2_out, C);
  not not_3 (not_3_out, B);
  not not_4 (not_4_out, C);
  and and_1 (and_1_out, not_1_out, not_2_out);
  not not_5 (not_5_out, D);
  not not_6 (not_6_out, A);
  and and_2 (and_2_out, not_3_out, C);
  and and_3 (and_3_out, B, not_4_out);
  not not_7 (not_7_out, D);
  and and_4 (and_4_out, B, C);
  not not_8 (not_8_out, E);
  and and_5 (and_5_out, and_1_out, not_5_out);
  or or_1 (or_1_out, and_5_out, and_6_out);
  and and_6 (and_6_out, A, D);
  and and_7 (and_7_out, A, C);
  and and_8 (and_8_out, and_7_out, E);
  and and_9 (and_9_out, not_6_out, D);
  or or_2 (or_2_out, and_9_out, and_10_out);
  and and_10 (and_10_out, and_2_out, E);
  and and_11 (and_11_out, and_3_out, not_7_out);
  or or_3 (or_3_out, and_11_out, and_12_out);
  and and_12 (and_12_out, and_4_out, not_8_out);
  or or_4 (I, or_1_out, and_8_out);
  or or_5 (R, or_2_out, or_3_out);
endmodule

module Instruction_Addresses (
  input  [15:0] in_1
);
endmodule

module ALU (
  input  [15:0] Input_1,
  input  [15:0] Input_2,
  input  [4:0] Opcode,
  output [15:0] Output,
  output greater,
  output zero,
  output less,
  output notzero
);

  wire a_s_a_n_1_add, a_s_a_n_1_and, a_s_a_n_1_nor, a_s_a_n_1_sub;
  wire [15:0] adder_1_out, and_1_out, nor_1_out, subtractor_1_out;

  a_s_a_n a_s_a_n_1 (
    .a(Opcode[4]), .b(Opcode[3]), .c(Opcode[2]), .d(Opcode[1]), .e(Opcode[0]), .add(a_s_a_n_1_add),
    .sub(a_s_a_n_1_sub), .\and (a_s_a_n_1_and), .\nor (a_s_a_n_1_nor));
  Adder #(.width(16)) adder_1 (.a(Input_1), .b(Input_2), .out(adder_1_out));  // open: cin, cout
  Subtractor #(.width(16)) subtractor_1 (.a(Input_1), .b(Input_2), .out(subtractor_1_out));  // open: bin, bout
  assign and_1_out = Input_1 & Input_2;  // AND_Gate and_1, 16 bits wide
  assign nor_1_out = ~(Input_1 | Input_2);  // NOR_Gate nor_1, 16 bits wide
  assign Output = a_s_a_n_1_add ? adder_1_out : 16'bz;  // Controlled_Buffer controlled_buffer_1
  assign Output = a_s_a_n_1_sub ? subtractor_1_out : 16'bz;  // Controlled_Buffer controlled_buffer_2
  assign Output = a_s_a_n_1_and ? and_1_out : 16'bz;  // Controlled_Buffer controlled_buffer_3
  assign Output = a_s_a_n_1_nor ? nor_1_out : 16'bz;  // Controlled_Buffer controlled_buffer_4
  Comparator #(.width(16)) comparator_1 (.a(Input_1), .b({16{1'b0}}), .gt(greater), .eq(zero), .lt(less));
  not not_1 (notzero, zero);
endmodule

module Register_File (
  input  WriteEnable,
  input  [2:0] ReadRegister1,
  input  [2:0] ReadRegister2,
  input  [2:0] Write_Register,
  input  [15:0] WriteData,
  input  clock,
  output [15:0] Read_Data1,
  output [15:0] Read_Data2
);

  wire button_1_out, demultiplexer_1_out0, demultiplexer_1_out1, demultiplexer_1_out2, demultiplexer_1_out3,
       demultiplexer_1_out4, demultiplexer_1_out5, demultiplexer_1_out6;
  wire [15:0] register_1_q, register_2_q, register_3_q, register_4_q, register_5_q, register_6_q,
       register_7_q, register_8_q;

  Demultiplexer #(.select(3), .enable("false")) demultiplexer_1 (
    .out0(demultiplexer_1_out0), .out1(demultiplexer_1_out1), .out2(demultiplexer_1_out2),
    .out3(demultiplexer_1_out3), .out4(demultiplexer_1_out4), .out5(demultiplexer_1_out5),
    .out6(demultiplexer_1_out6), .out7(demultiplexer_1_out6), .in(WriteEnable), .sel(Write_Register));
  Register #(.width(16)) register_1 (
    .D(WriteData), .en(demultiplexer_1_out0), .Q(register_1_q), .clk(clock), .clr(button_1_out));
  Register #(.width(16)) register_2 (
    .D(WriteData), .en(demultiplexer_1_out1), .Q(register_2_q), .clk(clock), .clr(button_1_out));
  Register #(.width(16)) register_3 (
    .D(WriteData), .en(demultiplexer_1_out2), .Q(register_3_q), .clk(clock), .clr(button_1_out));
  Register #(.width(16)) register_4 (
    .D(WriteData), .en(demultiplexer_1_out3), .Q(register_4_q), .clk(clock), .clr(button_1_out));
  Register #(.width(16)) register_5 (
    .D(WriteData), .en(demultiplexer_1_out4), .Q(register_5_q), .clk(clock), .clr(button_1_out));
  Register #(.width(16)) register_6 (
    .D(WriteData), .en(demultiplexer_1_out5), .Q(register_6_q), .clk(clock), .clr(button_1_out));
  Register #(.width(16)) register_7 (
    .D(WriteData), .en(demultiplexer_1_out6), .Q(register_7_q), .clk(clock), .clr(button_1_out));
  Register #(.width(16)) register_8 (
    .D(WriteData), .en(demultiplexer_1_out6), .Q(register_8_q), .clk(clock), .clr(button_1_out));
  Multiplexer #(.select(3), .width(16), .enable("false")) multiplexer_1 (
    .in0(register_1_q), .in1(register_2_q), .in2(register_3_q), .in3(register_4_q), .in4(register_5_q),
    .in5(register_6_q), .in6(register_7_q), .in7(register_8_q), .out(Read_Data1), .sel(ReadRegister1));
  Multiplexer #(.select(3), .width(16), .enable("false")) multiplexer_2 (
    .in0(register_1_q), .in1(register_2_q), .in2(register_3_q), .in3(register_4_q), .in4(register_5_q),
    .in5(register_6_q), .in6(register_7_q), .in7(register_8_q), .out(Read_Data2), .sel(ReadRegister2));
  Button button_1 (.out(button_1_out));
endmodule

module a_s_a_n (
  input  a,
  input  b,
  input  c,
  input  d,
  input  e,
  output add,
  output sub,
  output \and ,
  output \nor 
);

  wire and_1_out, and_2_out, and_3_out, and_4_out, and_5_out, and_6_out, and_7_out, and_8_out, and_9_out,
       and_10_out, and_12_out, and_13_out, and_15_out, and_16_out, and_18_out, not_1_out, not_2_out,
       not_3_out, not_4_out, not_5_out, not_6_out, not_7_out, not_8_out, not_9_out, not_10_out, not_11_out,
       not_12_out, not_13_out, not_14_out, not_15_out, not_16_out;

  not not_1 (not_1_out, a);
  not not_2 (not_2_out, b);
  not not_3 (not_3_out, c);
  not not_4 (not_4_out, d);
  not not_5 (not_5_out, a);
  not not_6 (not_6_out, b);
  not not_7 (not_7_out, c);
  not not_8 (not_8_out, e);
  not not_9 (not_9_out, a);
  not not_10 (not_10_out, b);
  not not_11 (not_11_out, a);
  not not_12 (not_12_out, b);
  not not_13 (not_13_out, a);
  not not_14 (not_14_out, b);
  and and_1 (and_1_out, not_1_out, not_2_out);
  and and_2 (and_2_out, not_3_out, not_4_out);
  and and_3 (and_3_out, not_5_out, not_6_out);
  and and_4 (and_4_out, not_7_out, not_8_out);
  and and_5 (and_5_out, not_9_out, not_10_out);
  not not_15 (not_15_out, c);
  and and_6 (and_6_out, not_11_out, not_12_out);
  not not_16 (not_16_out, e);
  and and_7 (and_7_out, not_13_out, not_14_out);
  and and_8 (and_8_out, and_1_out, and_2_out);
  or or_1 (add, and_8_out, and_9_out);
  and and_9 (and_9_out, and_3_out, and_4_out);
  and and_10 (and_10_out, and_5_out, not_15_out);
  and and_11 (sub, and_10_out, and_12_out);
  and and_12 (and_12_out, d, e);
  and and_13 (and_13_out, and_6_out, c);
  and and_14 (\and , and_13_out, and_15_out);
  and and_15 (and_15_out, d, not_16_out);
  and and_16 (and_16_out, and_7_out, c);
  and and_17 (\nor , and_16_out, and_18_out);
  and and_18 (and_18_out, d, e);
endmodule

module ShiftSignal (
  input  a,
  input  b,
  input  c,
  input  d,
  output shift
);

  wire and_1_out, not_1_out, not_2_out;

  not not_1 (not_1_out, a);
  and and_1 (and_1_out, not_1_out, b);
  not not_2 (not_2_out, c);
  and and_2 (shift, and_1_out, not_2_out);
endmodule

module memorysignal (
  input  a,
  input  b,
  input  c,
  input  d,
  output shift
);

  wire and_1_out, and_2_out, not_1_out;

  not not_1 (not_1_out, a);
  and and_1 (and_1_out, not_1_out, b);
  and and_2 (and_2_out, c, d);
  and and_3 (shift, and_1_out, and_2_out);
endmodule

module halt (
  input  a,
  input  b,
  input  c,
  input  d,
  input  e,
  output shift
);

  wire and_1_out, and_2_out, and_4_out, not_1_out, not_2_out, not_3_out;

  not not_1 (not_1_out, a);
  not not_2 (not_2_out, b);
  and and_1 (and_1_out, not_1_out, not_2_out);
  not not_3 (not_3_out, d);
  and and_2 (and_2_out, and_1_out, c);
  and and_3 (shift, and_2_out, and_4_out);
  and and_4 (and_4_out, not_3_out, e);
endmodule

module putsignal (
  input  a,
  input  b,
  input  c,
  input  d,
  input  e,
  output shift
);

  wire and_1_out, and_2_out, not_1_out, not_2_out;

  not not_1 (not_1_out, c);
  not not_2 (not_2_out, d);
  and and_1 (and_1_out, a, b);
  and and_2 (and_2_out, not_1_out, not_2_out);
  and and_3 (shift, and_1_out, and_2_out);
endmodule

// Control 1
module Control2 (
  input  [15:0] in_1,
  input  [3:0] in_2,
  output Immediate,
  output PC,
  output RS,
  output shamt,
  output writeenable
);

  wire branch_1_out, jump_1_jump, jumpregister_1_out;

  BLU blu_1 (
    .a(in_1[15]), .b(in_1[14]), .c(in_1[13]), .d(in_1[12]), .e(in_1[0]), .f(in_2[0]), .g(in_2[1]),
    .h(in_2[2]), .i(in_2[3]), .imm(Immediate), .pc(PC), .rs(RS));
  jumpregister jumpregister_1 (
    .a(in_1[15]), .b(in_1[14]), .c(in_1[13]), .d(in_1[12]), .e(in_1[0]), .out(jumpregister_1_out));
  shamt_rt shamt_rt_1 (.a(in_1[15]), .b(in_1[14]), .c(in_1[13]), .d(in_1[12]), .e(in_1[0]), .answer(shamt));
  writeenable writeenable_1 (.a(in_1[15]), .b(in_1[14]), .c(in_1[13]), .d(in_1[12]), .e(in_1[0]), .out(writeenable));
  branch branch_1 (.a(in_1[15]), .b(in_1[14]), .c(in_1[13]), .d(in_1[12]), .out(branch_1_out));
  Jump jump_1 (.a(in_1[15]), .b(in_1[14]), .c(in_1[13]), .d(in_1[12]), .e(in_1[0]), .jump(jump_1_jump));
endmodule

module shamt_rt (
  input  a,
  input  b,
  input  c,
  input  d,
  input  e,
  output answer
);

  wire and_1_out, and_2_out, not_1_out, not_2_out, not_3_out;

  not not_1 (not_1_out, a);
  not not_2 (not_2_out, c);
  not not_3 (not_3_out, e);
  and and_1 (and_1_out, not_1_out, b);
  and and_2 (and_2_out, not_2_out, not_3_out);
  and and_3 (answer, and_1_out, and_2_out);
endmodule

module writeenable (
  input  a,
  input  b,
  input  c,
  input  d,
  input  e,
  output out
);

  wire and_1_out, and_2_out, and_3_out, and_4_out, and_5_out, and_6_out, and_7_out, and_8_out, and_9_out,
       not_1_out, not_2_out, not_3_out, not_4_out, not_5_out, not_6_out, not_7_out, or_1_out, or_3_out;

  not not_1 (not_1_out, a);
  not not_2 (not_2_out, b);
  not not_3 (not_3_out, a);
  and and_1 (and_1_out, a, b);
  not not_4 (not_4_out, d);
  not not_5 (not_5_out, a);
  not not_6 (not_6_out, c);
  and and_2 (and_2_out, not_1_out, not_2_out);
  and and_3 (and_3_out, not_3_out, d);
  not not_7 (not_7_out, e);
  and and_4 (and_4_out, and_1_out, c);
  and and_5 (and_5_out, not_4_out, e);
  and and_6 (and_6_out, not_5_out, not_6_out);
  and and_7 (and_7_out, and_2_out, d);
  and and_8 (and_8_out, and_3_out, not_7_out);
  and and_9 (and_9_out, and_4_out, and_5_out);
  or or_1 (or_1_out, and_6_out, and_7_out);
  or or_2 (out, or_1_out, or_3_out);
  or or_3 (or_3_out, and_8_out, and_9_out);
endmodule

module branchcondition (
  input  a,
  input  b,
  input  c,
  input  d,
  output branch
);

  wire and_1_out, not_1_out, not_2_out;

  and and_1 (and_1_out, a, not_1_out);
  not not_1 (not_1_out, b);
  not not_2 (not_2_out, c);
  and and_2 (branch, and_1_out, not_2_out);
endmodule

module branch (
  input  a,
  input  b,
  input  c,
  input  d,
  output out
);

  wire and_1_out, not_1_out, not_2_out;

  and and_1 (and_1_out, a, not_1_out);
  not not_1 (not_1_out, b);
  not not_2 (not_2_out, c);
  and and_2 (out, and_1_out, not_2_out);
endmodule

module Jump (
  input  a,
  input  b,
  input  c,
  input  d,
  input  e,
  output jump
);

  wire and_1_out, and_2_out, and_3_out, and_4_out, and_5_out, and_6_out, and_7_out, not_1_out, not_2_out;

  not not_1 (not_1_out, c);
  and and_1 (and_1_out, a, b);
  not not_2 (not_2_out, d);
  and and_2 (and_2_out, a, b);
  and and_3 (and_3_out, not_1_out, d);
  and and_4 (and_4_out, and_1_out, c);
  and and_5 (and_5_out, not_2_out, e);
  and and_6 (and_6_out, and_2_out, and_3_out);
  and and_7 (and_7_out, and_4_out, and_5_out);
  or or_1 (jump, and_6_out, and_7_out);
endmodule

module jumpregister (
  input  a,
  input  b,
  input  c,
  input  d,
  input  e,
  output out
);

  wire and_1_out, and_2_out, and_3_out, not_1_out, not_2_out;

  and and_1 (and_1_out, a, b);
  not not_1 (not_1_out, d);
  not not_2 (not_2_out, e);
  and and_2 (and_2_out, and_1_out, c);
  and and_3 (and_3_out, not_1_out, not_2_out);
  and and_4 (out, and_2_out, and_3_out);
endmodule

module Control_3 (
  input  [15:0] in_1,
  output [4:0] out_2,
  output store,
  output load,
  output jumpandlink,
  output shiftright,
  output _0sign
);

  store store_1 (.a(in_1[15]), .b(in_1[14]), .c(in_1[13]), .d(in_1[12]), .e(in_1[0]), .out(store));
  load load_1 (.a(in_1[15]), .b(in_1[14]), .c(in_1[13]), .d(in_1[12]), .e(in_1[0]), .out(load));
  jumpandlink jumpandlink_1 (.a(in_1[15]), .b(in_1[14]), .c(in_1[13]), .d(in_1[12]), .e(in_1[0]), .out(jumpandlink));
  shiftright shiftright_1 (.a(in_1[15]), .b(in_1[14]), .c(in_1[13]), .d(in_1[12]), .e(in_1[0]), .out(shiftright));
  _0sign u_0sign_1 (.a(in_1[15]), .b(in_1[14]), .c(in_1[13]), .d(in_1[12]), .e(in_1[0]), .out(_0sign));

  assign out_2 = {in_1[15:12], in_1[0]};
endmodule

module store (
  input  a,
  input  b,
  input  c,
  input  d,
  input  e,
  output out
);

  wire and_1_out, and_2_out, and_4_out, not_1_out;

  not not_1 (not_1_out, a);
  and and_1 (and_1_out, not_1_out, b);
  and and_2 (and_2_out, and_1_out, c);
  and and_3 (out, and_2_out, and_4_out);
  and and_4 (and_4_out, d, e);
endmodule

module load (
  input  a,
  input  b,
  input  c,
  input  d,
  input  e,
  output out
);

  wire and_1_out, and_2_out, and_4_out, not_1_out, not_2_out;

  not not_1 (not_1_out, a);
  and and_1 (and_1_out, not_1_out, b);
  not not_2 (not_2_out, e);
  and and_2 (and_2_out, and_1_out, c);
  and and_3 (out, and_2_out, and_4_out);
  and and_4 (and_4_out, d, not_2_out);
endmodule

module jumpandlink (
  input  a,
  input  b,
  input  c,
  input  d,
  input  e,
  output out
);

  wire and_1_out, and_2_out, and_3_out, not_1_out;

  and and_1 (and_1_out, a, b);
  not not_1 (not_1_out, d);
  and and_2 (and_2_out, and_1_out, c);
  and and_3 (and_3_out, not_1_out, e);
  and and_4 (out, and_2_out, and_3_out);
endmodule

module shiftright (
  input  a,
  input  b,
  input  c,
  input  d,
  input  e,
  output out
);

  wire and_1_out, and_2_out, not_1_out, not_2_out;

  not not_1 (not_1_out, a);
  not not_2 (not_2_out, c);
  and and_1 (and_1_out, not_1_out, b);
  and and_2 (and_2_out, not_2_out, d);
  and and_3 (out, and_1_out, and_2_out);
endmodule

module _0sign (
  input  a,
  input  b,
  input  c,
  input  d,
  input  e,
  output out
);

  wire not_1_out, not_2_out, not_3_out, not_4_out, not_5_out;

  not not_1 (not_1_out, a);
  not not_2 (not_2_out, b);
  not not_3 (not_3_out, c);
  not not_4 (not_4_out, d);
  not not_5 (not_5_out, e);
  and and_1 (out, not_1_out, not_2_out, not_3_out, not_4_out, not_5_out);
endmodule

module comparator_logic (
  input  [7:0] in_1,
  input  [7:0] in_2,
  input  [7:0] in_3,
  output [1:0] out_4
);

  wire [2:0] comparator_1_eq;

  Comparator comparator_1 (.a(in_1), .b(in_2), .eq(comparator_1_eq[0]));  // open: gt, lt
  Comparator comparator_2 (.a(in_2), .b(in_3), .eq(comparator_1_eq[1]));  // open: gt, lt
  Comparator comparator_3 (.a(in_3), .b(in_1), .eq(comparator_1_eq[2]));  // open: gt, lt
  \logic  logic_1 (.in_1(comparator_1_eq), .out_2(out_4));
endmodule

module \logic  (
  input  [2:0] in_1,
  output [1:0] out_2
);

  wire comparator_1_eq, comparator_2_eq, comparator_3_eq, comparator_4_eq;

  Comparator #(.width(3)) comparator_1 (.a(in_1), .b(3'b111), .eq(comparator_1_eq));  // open: gt, lt
  Comparator #(.width(3)) comparator_2 (.a(in_1), .b(3'b101), .eq(comparator_2_eq));  // open: gt, lt
  Comparator #(.width(3)) comparator_3 (.a(in_1), .b(3'b110), .eq(comparator_3_eq));  // open: gt, lt
  Comparator #(.width(3)) comparator_4 (.a(in_1), .b(3'b011), .eq(comparator_4_eq));  // open: gt, lt
  assign out_2 = comparator_1_eq ? 2'b00 : 2'bz;  // Controlled_Buffer controlled_buffer_1
  assign out_2 = comparator_2_eq ? 2'b01 : 2'bz;  // Controlled_Buffer controlled_buffer_2
  assign out_2 = comparator_3_eq ? 2'b10 : 2'bz;  // Controlled_Buffer controlled_buffer_3
  assign out_2 = comparator_4_eq ? 2'b11 : 2'bz;  // Controlled_Buffer controlled_buffer_4
endmodule

module BLU (
  input  a,
  input  b,
  input  c,
  input  d,
  input  e,
  input  f,
  input  g,
  input  h,
  input  i,
  output imm,
  output pc,
  output rs
);

  wire and_1_out, and_2_out, and_3_out, and_4_out, and_5_out, and_6_out, and_7_out, and_8_out, and_9_out,
       and_10_out, and_11_out, and_12_out, and_13_out, and_14_out, and_15_out, and_16_out, and_17_out,
       and_18_out, and_19_out, and_20_out, and_21_out, and_22_out, and_23_out, and_24_out, and_25_out,
       and_26_out, and_27_out, and_28_out, and_29_out, and_30_out, and_31_out, and_32_out, and_33_out,
       and_34_out, and_35_out, and_36_out, and_37_out, and_38_out, and_39_out, and_40_out, and_41_out,
       and_42_out, and_43_out, and_44_out, and_45_out, and_46_out, and_47_out, and_48_out, and_49_out,
       and_50_out, and_51_out, and_53_out, and_54_out, and_55_out, and_56_out, and_57_out, and_58_out,
       and_59_out, not_1_out, not_2_out, not_3_out, not_4_out, not_5_out, not_6_out, not_7_out, not_8_out,
       not_9_out, not_10_out, not_11_out, not_12_out, not_13_out, not_14_out, not_15_out, not_16_out,
       not_17_out, not_18_out, not_19_out, not_20_out, not_21_out, not_22_out, not_23_out, not_24_out,
       not_25_out, not_26_out, not_27_out, not_28_out, not_29_out, not_30_out, not_31_out, not_32_out,
       not_33_out, not_34_out, not_35_out, or_1_out, or_2_out, or_3_out, or_4_out, or_5_out, or_6_out,
       or_7_out, or_8_out, or_9_out, or_10_out, or_11_out, or_12_out, or_13_out;

  not not_1 (not_1_out, b);
  not not_2 (not_2_out, d);
  not not_3 (not_3_out, e);
  not not_4 (not_4_out, b);
  not not_5 (not_5_out, d);
  not not_6 (not_6_out, b);
  not not_7 (not_7_out, e);
  and and_1 (and_1_out, a, b);
  not not_8 (not_8_out, d);
  not not_9 (not_9_out, e);
  and and_2 (and_2_out, a, not_1_out);
  not not_10 (not_10_out, c);
  and and_3 (and_3_out, not_2_out, not_3_out);
  and and_4 (and_4_out, a, not_4_out);
  not not_11 (not_11_out, c);
  and and_5 (and_5_out, not_5_out, e);
  not not_12 (not_12_out, c);
  not not_13 (not_13_out, c);
  not not_14 (not_14_out, b);
  not not_15 (not_15_out, d);
  not not_16 (not_16_out, e);
  not not_17 (not_17_out, f);
  and and_6 (and_6_out, not_6_out, not_7_out);
  not not_18 (not_18_out, f);
  not not_19 (not_19_out, g);
  not not_20 (not_20_out, h);
  not not_21 (not_21_out, c);
  not not_22 (not_22_out, d);
  not not_23 (not_23_out, g);
  not not_24 (not_24_out, b);
  not not_25 (not_25_out, i);
  not not_26 (not_26_out, c);
  and and_7 (and_7_out, and_1_out, c);
  and and_8 (and_8_out, not_8_out, not_9_out);
  and and_9 (and_9_out, and_2_out, not_10_out);
  and and_10 (and_10_out, and_9_out, and_11_out);
  and and_11 (and_11_out, and_3_out, f);
  and and_12 (and_12_out, and_4_out, not_11_out);
  and and_13 (and_13_out, and_12_out, and_14_out);
  and and_14 (and_14_out, and_5_out, g);
  and and_15 (and_15_out, a, not_12_out);
  and and_16 (and_16_out, and_15_out, d);
  not not_27 (not_27_out, e);
  and and_17 (and_17_out, not_27_out, h);
  and and_18 (and_18_out, a, not_13_out);
  and and_19 (and_19_out, and_18_out, d);
  and and_20 (and_20_out, e, i);
  and and_21 (and_21_out, a, b);
  and and_22 (and_22_out, and_21_out, not_28_out);
  not not_28 (not_28_out, c);
  and and_23 (and_23_out, d, i);
  and and_24 (and_24_out, a, b);
  and and_25 (and_25_out, and_24_out, not_29_out);
  not not_29 (not_29_out, c);
  and and_26 (and_26_out, d, g);
  and and_27 (and_27_out, a, b);
  and and_28 (and_28_out, and_27_out, not_30_out);
  not not_30 (not_30_out, c);
  and and_29 (and_29_out, d, f);
  and and_30 (and_30_out, a, b);
  and and_31 (and_31_out, and_30_out, not_31_out);
  not not_31 (not_31_out, c);
  and and_32 (and_32_out, d, e);
  and and_33 (and_33_out, a, b);
  and and_34 (and_34_out, and_33_out, c);
  not not_32 (not_32_out, d);
  and and_35 (and_35_out, not_32_out, e);
  not not_33 (not_33_out, a);
  and and_36 (and_36_out, not_14_out, not_15_out);
  and and_37 (and_37_out, and_36_out, and_38_out);
  and and_38 (and_38_out, not_16_out, not_17_out);
  and and_39 (and_39_out, and_6_out, not_18_out);
  and and_40 (and_40_out, and_39_out, and_41_out);
  and and_41 (and_41_out, not_19_out, not_20_out);
  and and_42 (and_42_out, not_21_out, not_22_out);
  and and_43 (and_43_out, and_42_out, and_44_out);
  and and_44 (and_44_out, e, not_23_out);
  and and_45 (and_45_out, not_24_out, d);
  and and_46 (and_46_out, and_45_out, and_47_out);
  and and_47 (and_47_out, e, not_25_out);
  not not_34 (not_34_out, b);
  and and_48 (and_48_out, not_34_out, c);
  and and_49 (and_49_out, c, d);
  and and_50 (and_50_out, b, not_26_out);
  and and_51 (and_51_out, and_50_out, not_35_out);
  not not_35 (not_35_out, d);
  and and_52 (rs, and_7_out, and_8_out);
  or or_1 (or_1_out, and_10_out, and_13_out);
  and and_53 (and_53_out, and_16_out, and_17_out);
  and and_54 (and_54_out, and_19_out, and_20_out);
  and and_55 (and_55_out, and_22_out, and_23_out);
  and and_56 (and_56_out, and_25_out, and_26_out);
  and and_57 (and_57_out, and_28_out, and_29_out);
  and and_58 (and_58_out, and_31_out, and_32_out);
  and and_59 (and_59_out, and_34_out, and_35_out);
  or or_2 (or_2_out, not_33_out, and_37_out);
  or or_3 (or_3_out, and_40_out, and_43_out);
  or or_4 (or_4_out, and_46_out, and_48_out);
  or or_5 (or_5_out, and_49_out, and_51_out);
  or or_6 (or_6_out, or_1_out, and_53_out);
  or or_7 (or_7_out, and_54_out, and_55_out);
  or or_8 (or_8_out, and_56_out, and_57_out);
  or or_9 (or_9_out, and_58_out, and_59_out);
  or or_10 (or_10_out, or_2_out, or_3_out);
  or or_11 (or_11_out, or_4_out, or_5_out);
  or or_12 (or_12_out, or_6_out, or_7_out);
  or or_13 (or_13_out, or_8_out, or_9_out);
  or or_14 (pc, or_10_out, or_11_out);
  or or_15 (imm, or_12_out, or_13_out);
endmodule
