// Logisim project lab10part2.circ as structural Verilog: 2 circuits, main circuit GrayCode
module main (
  input  [3:0] Input,
  output x2,
  output x1,
  output x0
);

  GrayCode graycode_1 (.\input (Input), .X2(x2), .X1(x1), .X0(x0));
endmodule

module GrayCode (
  input  [3:0] \input ,
  output X2,
  output X1,
  output X0
);

  wire and_1_out, and_2_out, and_3_out, and_4_out, and_5_out, and_6_out, and_7_out, and_8_out, not_1_out,
       not_2_out, not_3_out, not_4_out, or_1_out, or_2_out, or_3_out, or_4_out, or_7_out, xor_1_out,
       xor_2_out;

  not not_1 (not_1_out, \input [3]);
  not not_2 (not_2_out, \input [1]);
  not not_3 (not_3_out, \input [0]);
  not not_4 (not_4_out, \input [2]);
  or or_1 (or_1_out, \input [0], \input [1]);
  and and_1 (and_1_out, or_1_out, and_2_out);
  and and_2 (and_2_out, \input [2], \input [3]);
  and and_3 (and_3_out, \input [0], \input [1]);
  and and_4 (and_4_out, and_3_out, or_2_out);
  or or_2 (or_2_out, \input [2], \input [3]);
  and and_5 (and_5_out, not_1_out, xor_1_out);
  xor xor_1 (xor_1_out, \input [0], \input [1]);
  xor xor_2 (xor_2_out, \input [1], \input [2]);
  or or_3 (or_3_out, not_3_out, not_1_out);
  or or_4 (or_4_out, not_3_out, not_2_out);
  and and_6 (and_6_out, not_4_out, \input [3]);
  and and_7 (and_7_out, xor_2_out, or_3_out);
  and and_8 (and_8_out, or_4_out, and_6_out);
  or or_5 (X2, and_1_out, and_4_out);
  or or_6 (X1, and_5_out, or_7_out);
  or or_7 (or_7_out, and_7_out, and_8_out);

  assign X0 = 1'b0;
endmodule
