// Logisim project lab11part2.circ as structural Verilog: 1 circuit, main circuit main
module main (
);

  wire clear_out, clock_1_out, d_ff_1_q, not_1_out;
  wire [7:0] counter_1_q, ram_1_data;

  Clock clock_1 (.out(clock_1_out));
  Counter counter_1 (.Q(counter_1_q), .clk(clock_1_out), .clr(clear_out));  // open: load, D, count, carry
  RAM ram_1 (.addr(counter_1_q), .data(ram_1_data), .clk(clock_1_out), .ld(d_ff_1_q), .clr(clear_out));  // open: sel
  Button clear (.out(clear_out));
  Comparator comparator_1 (.a(counter_1_q), .b({8{1'b1}}), .eq(clear_out));  // open: gt, lt
  assign ram_1_data = not_1_out ? 8'h61 : 8'bz;  // Controlled_Buffer controlled_buffer_1
  not not_1 (not_1_out, d_ff_1_q);
  D_Flip_Flop d_ff_1 (.clk(clock_1_out), .D(clear_out), .Q(d_ff_1_q), .en(clear_out));  // open: Qn, preset, reset
endmodule
